# Fritzing sketch homeassistant esp32 shtc3 adafruit connection (saved by Fritzing 0.9.3b)

parts:
  Part1 = Adafruit SHTC3 STEMMA QT [part_number="Adafruit #4636"]
  M1 = DOIT Esp32 DevKit v1 (30 pins long, 11 pins width) [part_number=ESP32S-PIN30]

nets:
  VCC: Part1.VCC, M1.3V3
  GND: Part1.GND, M1.GND
  N1: Part1.SCL, M1.D22
  N2: Part1.SDA, M1.D21

custom parts:
  Adafruit SHTC3 STEMMA QT: Sensirion Temperature/Humidity sensors are some of the finest & highest-accuracy devices you can get. And finally, we have some that have a true I2C interface for easy reading. The SHTC3 sensor has an excellent ±2% relative humidity and ±0.2 °C accuracy for most uses. Unlike some earlier SHT sensors, this sensor has a true I2C interface on address 0x70. Unlike some earlier SHT sensors, this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
  DOIT Esp32 DevKit v1 (30 pins long, 11 pins width): The DOIT Esp32 DevKit v1 is one of the development board created by DOIT to evaluate the ESP-WROOM-32 module. It is based on the ESP32 microcontroller that boasts Wifi, Bluetooth, Ethernet and Low Power support all in a single chip. (vanepp) made breadboard work, adjusted pin numbering and labels and reduced size of schematic and cleaned up pcb. This chip is 30pins long (2 x15) and 11 pins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
